# Fritzing sketch OnOff_Motor_P01_V03 프리츠 (saved by Fritzing 0.9.10b)
breadboards: 1

parts:
  RHT1 = Humidity and Temperature Sensor RHT03
  Grove1 = Grove OLED 128x96
  부품1 = Arduino Nano (Rev3.0)
  M1 = DC Motor [voltage_(max)=6V voltage_(min)=3V]
  U1 = L9110 H-bridge module [part_number="L9110 H-bridge"]
  M2 = DC Motor [voltage_(max)=6V voltage_(min)=3V]
  Power_plug1 = Power plug
  R1 = TRIMPOT [maximum_resistance=10kΩ knob_status=50% power=0.5W package=trimpot_pth_s3_lock]
  R2 = TRIMPOT [maximum_resistance=10kΩ knob_status=50% power=0.5W package=trimpot_pth_s3_lock]

nets:
  VCC: RHT1.Vcc, Grove1.VCC, 부품1.3V3
  N1: RHT1.RX, 부품1.D12/MISO
  GND: RHT1.GND_2, Grove1.GND, 부품1.GND, U1.GND, Power_plug1.GND, R1.CCW, R2.CCW
  N2: Grove1.SDA, 부품1.A4
  N3: Grove1.SCL, 부품1.A5
  N4: 부품1.D5, U1.A-IA
  N5: 부품1.D6, U1.A-IB
  N6: 부품1.D10, U1.B-IA
  N7: 부품1.D11/MOSI, U1.B-IB
  N8: 부품1.5V, R1.CW, R2.CW
  N9: 부품1.A1, R2.WIPER
  N10: 부품1.A0, R1.WIPER
  N11: M1.pin_1, U1.MOTOR_B-B
  N12: M1.pin_2, U1.MOTOR_B-A
  VCC_2: U1.VCC, Power_plug1.VCC
  N13: U1.MOTOR_A-A, M2.pin_2
  N14: U1.MOTOR_A-B, M2.pin_1

notes:
  12v
  수중모터 12v 5W
  DHT22
  OLED I2C

custom parts:
  Humidity and Temperature Sensor RHT03: Digital relative humidity & temperature sensor RHT03
